# Fritzing sketch pin (saved by Fritzing 0.9.3b)

parts:
  Часть1 = Arduino Nano (Rev3.0)
  HC-SR04_Sensor_1 = HC-SR04 Ultrasonic Distance Sensor
  J1 = Basic Servo
  J2 = Basic Servo
  R1 = Resistor [tolerance=±5% resistance=21 package=THT]
  LD2 = LD
  X1 = USB Connectors [package=usb-a-h]
  S1 = SWITCH-MOMENTARY-2 [package=tactile_switch_tall]
  LD3 = LD
  LD4 = LD

nets:
  GND: Часть1.GND, J1.gnd, J2.gnd, X1.GND, S1.1
  N1: Часть1.D4, S1.2
  N2: Часть1.D5, R1.Pin_1
  N3: Часть1.D7, J2.pulse
  N4: Часть1.D9, J1.pulse
  N5: Часть1.D11/MOSI, HC-SR04_Sensor_1.ECHO
  N6: Часть1.D12/MISO, HC-SR04_Sensor_1.TRIG
  VCC: Часть1.5V, HC-SR04_Sensor_1.VCC, J1.vcc, J2.vcc, X1.D+
  N7: HC-SR04_Sensor_1.GND, LD2.cathode, LD3.cathode, LD4.cathode

notes:
  Внешнее питание:
  USB порт
  Лазер 5V
  Резистор
  21 Ом

custom parts:
  LD: A Generic Red Dot Laser Diode Module (~5mW)
